# Fritzing sketch micromouse (saved by Fritzing 0.9.3b)
circuit board: 8cm x 7.7cm
breadboards: 1

parts:
  Arduino = Arduino Uno (Rev3)
  Buzzer = Piezo Speaker - PC Mount [part_number=COM-07950]
  Boton_1 = Pushbutton [package=THT]
  Res_1 = Resistor [tolerance=±5% resistance=220 package=THT]
  Boton_2 = Pushbutton [package=THT]
  Res_2 = Resistor [tolerance=±5% resistance=220 package=THT]
  LED = LED - 5mm [color="Red (633nm)" package="5 mm [THT]"]
  Ultrasonico_1 = hc-sr04
  Ultrasonico_3 = hc-sr04
  Encoder_1 = Generic male header - 4 pins [form="♂ (male)" package=THT]
  Encoder_2 = Generic male header - 4 pins [form="♂ (male)" package=THT]
  Ultrasonico_2 = hc-sr04

nets:
  N1: Arduino.A0, Ultrasonico_1.Trig
  N2: Arduino.A1, Ultrasonico_1.Echo
  N3: Arduino.A2, Ultrasonico_2.Echo
  N4: Arduino.A3, Ultrasonico_2.Trig
  N5: Arduino.A4/SDA, Ultrasonico_3.Echo
  N6: Arduino.A5/SCL, Ultrasonico_3.Trig
  N7: Arduino.D11_PWM/MOSI, Boton_2.leg1, Res_2.Pin_0
  N8: Arduino.D12/MISO, LED.anode
  N9: Arduino.D13/SCK, Buzzer.VCC
  GND: Arduino.GND, Buzzer.GND, Res_1.Pin_1, Res_2.Pin_1, LED.cathode, Ultrasonico_1.GND, Ultrasonico_3.GND, Encoder_1.GND, Encoder_2.GND, Ultrasonico_2.GND
  N10: Arduino.D2, Encoder_1.OUT_A
  N11: Arduino.D3_PWM, Encoder_2.OUT_A
  N12: Arduino.D4, Encoder_1.OUT_B
  N13: Arduino.D5_PWM, Encoder_2.OUT_B
  N14: Arduino.D6_PWM, Boton_1.leg1, Res_1.Pin_0
  VCC: Arduino.5V, Boton_1.leg0, Boton_2.leg0, Ultrasonico_1.VCC, Ultrasonico_3.VCC, Encoder_1.VCC, Encoder_2.VCC, Ultrasonico_2.VCC

notes:
  El Retornno De Bob I
  gnd

custom parts:
  Piezo Speaker - PC Mount: This is a small 12mm round speaker that operates around the audible 2kHz range. You can use these speakers to create simple music or user interfaces. Each speaker is PTH solderable and requires an operating voltage of 3.5-5V with a mean current of 35mA max. These speakers also have a typical sound output of 95 dBA and a coil resistance of 42 ±6.3 ohms.
  Generic male header - 4 pins: Generic male header
