# Fritzing sketch microperfe (saved by Fritzing 0.9.3b)
circuit board: 8cm x 7.7cm
breadboards: 1

parts:
  Buzzer = Piezo Speaker - PC Mount [part_number=COM-07950]
  Boton_1 = Pushbutton [package=THT]
  Res_1 = Resistor [tolerance=±5% resistance=220 package=THT]
  Boton_2 = Pushbutton [package=THT]
  Res_2 = Resistor [tolerance=±5% resistance=220 package=THT]
  LED = LED - 5mm [color="Red (633nm)" package="5 mm [THT]"]
  Ultrasonico_1 = hc-sr04
  Ultrasonico_3 = hc-sr04
  Encoder_1 = Generic male header - 4 pins [form="♂ (male)" package=THT]
  Encoder_2 = Generic male header - 4 pins [form="♂ (male)" package=THT]
  Ultrasonico_2 = hc-sr04
  J1 = male pin header, 6 pins [form="♂ (male)"]
  J2 = male pin header, 8 pins [form="♂ (male)"]
  J3 = male pin header, 8 pins [form="♂ (male)"]
  J4 = male pin header, 10 pins [form="♂ (male)"]

nets:
  N1: Buzzer.GND, J2.pin6
  N2: Buzzer.VCC, J4.pin5
  VCC: Boton_1.leg0, Boton_2.leg0, Ultrasonico_1.VCC, Ultrasonico_3.VCC, Encoder_1.VCC, Encoder_2.VCC, Ultrasonico_2.VCC, J2.pin5
  N3: Boton_1.leg1, Res_1.Pin_0, J3.pin2
  N4: Res_1.Pin_1, Encoder_1.GND, J2.pin7
  N5: Boton_2.leg1, Res_2.Pin_0, J4.pin7
  GND: Res_2.Pin_1, LED.cathode, Ultrasonico_1.GND, Ultrasonico_3.GND, Encoder_2.GND, Ultrasonico_2.GND, J4.pin4
  N6: LED.anode, J4.pin6
  N7: Ultrasonico_1.Trig, J1.pin1
  N8: Ultrasonico_1.Echo, J1.pin2
  N9: Ultrasonico_3.Trig, J1.pin6
  N10: Ultrasonico_3.Echo, J1.pin5
  N11: Encoder_1.OUT_B, J3.pin4
  N12: Encoder_1.OUT_A, J3.pin6
  N13: Encoder_2.OUT_B, J3.pin3
  N14: Encoder_2.OUT_A, J3.pin5
  N15: Ultrasonico_2.Trig, J1.pin4
  N16: Ultrasonico_2.Echo, J1.pin3

notes:
  El Retornno De Bob I
  gnd
  Arduino

custom parts:
  Piezo Speaker - PC Mount: This is a small 12mm round speaker that operates around the audible 2kHz range. You can use these speakers to create simple music or user interfaces. Each speaker is PTH solderable and requires an operating voltage of 3.5-5V with a mean current of 35mA max. These speakers also have a typical sound output of 95 dBA and a coil resistance of 42 ±6.3 ohms.
  Generic male header - 4 pins: Generic male header
